// Logisim project carrylookahead.circ as structural Verilog: 1 circuit, main circuit main
module main (
  input  C0,
  input  X0,
  input  Y0,
  input  X1,
  input  Y1,
  input  X2,
  input  Y2,
  input  X3,
  input  Y3,
  output out_10,
  output out_11,
  output out_12,
  output out_13
);

  wire C11_out, C12_out, C13_out, C21_out, C22_out, C31_out, G0_out, G1_out, G2_out, G3_out, P0_out,
       P0C0_out, P0C01_out, P0C02_out, P0C03_out, P1_out, P1C11_out, P1C12_out, P1C13_out, P2_out, P2C21_out,
       P2C22_out, P3_out, P3C31_out;
  wire [3:0] S0_out;

  and G1 (G1_out, X1, Y1);
  xor P0 (P0_out, X0, Y0);
  and G0 (G0_out, X0, Y0);
  xor P1 (P1_out, X1, Y1);
  xor P2 (P2_out, X2, Y2);
  and G2 (G2_out, X2, Y2);
  xor P3 (P3_out, X3, Y3);
  and G3 (G3_out, X3, Y3);
  and P0C0 (P0C0_out, C0, P0_out);
  and P0C01 (P0C01_out, P0_out, C0);
  and P0C02 (P0C02_out, C0, P0_out);
  and P0C03 (P0C03_out, P0_out, C0);
  or C11 (C11_out, G0_out, P0C01_out);
  or C13 (C13_out, P0C03_out, G0_out);
  and P1C11 (P1C11_out, C11_out, P1_out);
  or C12 (C12_out, G0_out, P0C02_out);
  and P2C21 (P2C21_out, C21_out, P2_out);
  and P1C13 (P1C13_out, C13_out, P1_out);
  and P1C12 (P1C12_out, P1_out, C12_out);
  and P3C31 (P3C31_out, C31_out, P3_out);
  xor S0 (S0_out[0], C0, P0_out);
  or C21 (C21_out, P1C12_out, G1_out);
  or C22 (C22_out, P1C13_out, G1_out);
  and P2C22 (P2C22_out, P2_out, C22_out);
  or C1 (out_10, P0C0_out, G0_out);
  or C2 (out_11, P1C11_out, G1_out);
  or C31 (C31_out, P2C22_out, G2_out);
  or C3 (out_12, P2C21_out, G2_out);
  xor S1 (S0_out[1], out_10, P1_out);
  xor S2 (S0_out[2], out_11, P2_out);
  xor S3 (S0_out[3], out_12, P3_out);
  or C4 (out_13, P3C31_out, G3_out);
  Hex_Digit_Display hex_digit_display_1 (.value(S0_out));  // open: dp
endmodule
